// Logisim project Main.circ as structural Verilog
module registerBank (
  input  [2:0] regLdS
);

  wire decoder_1_out0, decoder_1_out1, decoder_1_out2, decoder_1_out3, decoder_1_out4, decoder_1_out5;

  Decoder #(.select(3)) decoder_1 (
    .out0(decoder_1_out0), .out1(decoder_1_out1), .out2(decoder_1_out2), .out3(decoder_1_out3),
    .out4(decoder_1_out4), .out5(decoder_1_out5), .sel(regLdS), .en(1'b1));  // open: out6, out7
  Register #(.width(12)) AR (.en(decoder_1_out0));  // open: D, Q, clk, clr
  Register #(.width(12)) PC (.en(decoder_1_out1));  // open: D, Q, clk, clr
  Register #(.width(12)) SP (.en(decoder_1_out2));  // open: D, Q, clk, clr
  Register #(.width(16)) RR (.en(decoder_1_out3));  // open: D, Q, clk, clr
  Register #(.width(16)) IR (.en(decoder_1_out4));  // open: D, Q, clk, clr
  Register #(.width(16)) IR_2 (.en(decoder_1_out5));  // open: D, Q, clk, clr
  RAM #(.addrWidth(12), .dataWidth(16), .bus("separate")) ram_1 ();  // open: addr, din, data, str, sel, clk, ld, clr
endmodule
